# Fritzing sketch 2-x-x wiring (saved by Fritzing 0.9.6b)

parts:
  Part1 = Adafruit Feather RP2040 [part_number="Adafruit #4884"]
  Part7 = Adafruit DRV8833 DC/Stepper Motor Driver [part_number="Adafruit #3297"]
  Front_Motor1 = DC Motor
  Back_Motor1 = DC Motor
  Part8 = Adafruit VL53L0X Time of Flight Distance Sensor [part_number="Adafruit #3317"]
  Part9 = Adafruit APDS-9960 [part_number="Adafruit #3595"]
  U1 = SWITCH_SPDT [package=kps-1290]
  U2 = LIPO-110mAh [package=lipo-110]

nets:
  GND: Part1.GND, Part7.GND, Part8.GND, Part9.GND, U1.O, U2.-
  VIN: Part1.+3V3, Part8.VIN, Part9.VIN, U1.S
  N1: Part1.SDA, Part8.SDA, Part9.SDA
  N2: Part1.SCL, Part8.SCL, Part9.SCL
  N3: Part1.D24, U1.P
  N4: Part1.VBAT, Part7.VMOTOR, U2.+
  N5: Part1.D12, Part7.BIN2
  N6: Part1.D11, Part7.BIN1
  N7: Part1.D10, Part7.AIN2
  N8: Part1.D9, Part7.AIN1
  N9: Part7.AOUT2, Back_Motor1.pin_2
  N10: Part7.AOUT1, Back_Motor1.pin_1
  N11: Part7.BOUT1, Front_Motor1.pin_2
  N12: Part7.BOUT2, Front_Motor1.pin_1

custom parts:
  Adafruit Feather RP2040: A new chip means a new Feather, and the Raspberry Pi RP2040 is no exception. When we saw this chip we thought "this chip is going to be awesome when we give it the Feather Treatment" and so we did! This Feather features the RP2040, and all niceties you know and love about Feather Measures 2.0" x 0.9" x 0.28" (50.8mm x 22.8mm x 7mm) without headers soldered in Light as a (large?) feather - 5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
  Adafruit DRV8833 DC/Stepper Motor Driver: Spin two DC motors or step one bi-polar or uni-polar stepper with up to 1.2A per channel using the DRV8833. This motor driver chip is a nice alternative to the TB6612 driver. Like that chip, you get 2 full H-bridges, but this chip is better for low voltage uses (can run from 2.7V up to 10.8V motor power) and has built in current limiting capability. We set it up for 1A current limiting so you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
  Adafruit VL53L0X Time of Flight Distance Sensor: The VL53L0X is a Time of Flight distance sensor like no other you've used! The sensor contains a very tiny invisible laser source, and a matching sensor. The VL53L0X can detect the "time of flight", or how long the light has taken to bounce back to the sensor. Since it uses a very narrow light source, it is good for determining distance of only the surface directly in front of it. Unlike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
  Adafruit APDS-9960: The APDS9960 from Avago Technologies has an integrated IR LED and driver, along with four directional photodiodes that sense reflected IR energy from the LED. It's proximity detection feature allows it to measure the distance an object is from the front of the sensor (up to a few centimeters) with 8 bit resolution. Since there are four IR sensors, you can measure the changes in light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
