# Fritzing sketch Wiring sketch (saved by Fritzing 0.9.6b)
breadboards: 1

parts:
  Part1 = Adafruit QT Py [part_number="Adafruit #4600"]
  Part2 = Adafruit DRV8833 DC/Stepper Motor Driver [part_number="Adafruit #3297"]
  Part3 = Adafruit VL53L0X Time of Flight Distance Sensor [part_number="Adafruit #3317"]
  Part4 = Adafruit Pro Trinket LiIon/LiPoly Backpack [part_number="Adafruit #2124"]
  U1 = SWITCH_SPDT [package=kps-1290]
  D1 = Schottky Diode [part_number=1N5817 package="Melf DO-213 AB [SMD]"]
  M1 = DC Motor
  M2 = DC Motor
  U2 = LIPO-110mAh [package=lipo-110]  # not connected

nets:
  GND: Part1.GND, Part2.GND, Part3.GND, Part4.GND
  3.3V: Part1.3.3V, Part3.VIN
  N1: Part1.SDA, Part3.SDA
  N2: Part1.SCL, Part3.SCL
  N3: Part1.RX_A7, Part2.BIN2
  N4: Part1.SCK, Part2.BIN1
  N5: Part1.MISO, Part2.AIN2
  N6: Part1.MOSI, Part2.AIN1
  N7: Part1.+5V, Part2.VMOTOR, U1.P
  N8: Part2.AOUT2, M2.pin_2
  N9: Part2.AOUT1, M2.pin_1
  N10: Part2.BOUT1, M1.pin_2
  N11: Part2.BOUT2, M1.pin_1
  N12: Part4.VBUS, U1.S
  N13: Part4.VBAT, D1.anode
  N14: U1.O, D1.cathode

custom parts:
  Adafruit QT Py: What a cutie pie! Or is it... a QT Py? This diminutive dev board comes with our favorite lil chip, the SAMD21 (as made famous in our GEMMA M0 and Trinket M0 boards). This time it comes with our favorite connector - the STEMMA QT, a chainable I2C port that can be used with any of our STEMMA QT sensors and accessories. OLEDs! Inertial Measurment Units! Sensors a-plenty. All plug-and-play thanks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
  Adafruit DRV8833 DC/Stepper Motor Driver: Spin two DC motors or step one bi-polar or uni-polar stepper with up to 1.2A per channel using the DRV8833. This motor driver chip is a nice alternative to the TB6612 driver. Like that chip, you get 2 full H-bridges, but this chip is better for low voltage uses (can run from 2.7V up to 10.8V motor power) and has built in current limiting capability. We set it up for 1A current limiting so you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
  Adafruit VL53L0X Time of Flight Distance Sensor: The VL53L0X is a Time of Flight distance sensor like no other you've used! The sensor contains a very tiny invisible laser source, and a matching sensor. The VL53L0X can detect the "time of flight", or how long the light has taken to bounce back to the sensor. Since it uses a very narrow light source, it is good for determining distance of only the surface directly in front of it. Unlike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
  Adafruit Pro Trinket LiIon/LiPoly Backpack: If you have a Pro Trinket you probably know it's the perfect little size for a portable project. This LiPoly backpack makes it really easy to do! Instead of wiring 2 or 3 boards together to make a charging system, this little PCB sits on top of the Pro Trinket and allows a LiPoly/LiIon battery to plug in. When the Pro Trinket USB port is powered, the battery is recharged automatically. Unplug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
